# Fritzing sketch KentonControlV1 (saved by Fritzing 0.9.3b)
circuit board: 9.22cm x 4.97299cm
breadboards: 1

parts:
  MAX232 = RS232 Transceiver [package=dil16]
  6N138 = 6n137 Optocoupler [package="DIP (Dual Inline) [THT]"]
  D1 = Rectifier Diode [part_number=1N4001 package="300 mil [THT]"]
  R1_220Ω = Resistor [tolerance=±5% resistance=220 package=THT]
  DIN1_MIDI_In = DIN-5 jack (MIDI) [package=THT]
  DIN2_MIDI_Out = DIN-5 jack (MIDI) [package=THT]
  R2_220Ω = Resistor [tolerance=±5% resistance=220 package=THT]
  C4 = Ceramic Capacitor [capacitance=1µF voltage=50V package="100 mil [THT, multilayer]"]
  C3 = Ceramic Capacitor [capacitance=1µF voltage=50V package="100 mil [THT, multilayer]"]
  C2 = Ceramic Capacitor [capacitance=1µF voltage=50V package="100 mil [THT, multilayer]"]
  C5 = Ceramic Capacitor [capacitance=1µF voltage=50V package="100 mil [THT, multilayer]"]
  TX = Header 3 [package=molex-1x3_lock]
  R3_220Ω = Resistor [tolerance=±5% resistance=220 package=THT]
  5V_VCC = Header 3 [package=molex-1x3_lock]
  C1 = Ceramic Capacitor [capacitance=100nF package="100 mil [THT, multilayer]"]
  Arduino_Nano_Rev_3_or_4 = Arduino Nano (Rev3.0) (ICSP)
  S1_Reset = Pushbutton [package="[THT]"]
  S2_SetDIN48 = Pushbutton [package="[THT]"]
  S3_SetDIN24 = Pushbutton [package="[THT]"]
  S4_SetStart = Pushbutton [package="[THT]"]
  S5_SetStart1 = Pushbutton [package="[THT]"]
  S6_SetNoThru = Pushbutton [package="[THT]"]
  S7_SetThru = Pushbutton [package="[THT]"]
  S8_Restore = Pushbutton [package="[THT]"]

nets:
  N1: MAX232.C1+, C3.0
  N2: MAX232.V+, C2.1
  N3: MAX232.C1-, C3.1
  N4: MAX232.C2+, C4.0
  N5: MAX232.C2-, C4.1
  N6: MAX232.V-, C5.1
  GND: MAX232.R2IN, MAX232.T2IN, MAX232.GND, 6N138.NC, 6N138.GND, 6N138.Ve, C5.0, 5V_VCC.3, C1.1
  N7: MAX232.T1IN, 6N138.Vo, R2_220Ω.Pin_1
  N8: MAX232.R1OUT, DIN2_MIDI_Out.5
  N9: MAX232.R1IN, TX.3, Arduino_Nano_Rev_3_or_4.D1/TX
  N10: MAX232.T1OUT, TX.1, Arduino_Nano_Rev_3_or_4.D0/RX
  VCC: MAX232.VCC, 6N138.Vcc, R2_220Ω.Pin_0, C2.0, TX.2, R3_220Ω.Pin_0, 5V_VCC.1, C1.0, Arduino_Nano_Rev_3_or_4.5V
  N11: 6N138.Vf+, D1.cathode, DIN1_MIDI_In.4
  N12: 6N138.Vf-, D1.anode, R1_220Ω.Pin_0
  N13: R1_220Ω.Pin_1, DIN1_MIDI_In.5
  N14: DIN2_MIDI_Out.4, R3_220Ω.Pin_1
  N15: Arduino_Nano_Rev_3_or_4.GND, S1_Reset.Pin_3, S1_Reset.Pin_4, S2_SetDIN48.Pin_1, S2_SetDIN48.Pin_2, S3_SetDIN24.Pin_3, S3_SetDIN24.Pin_4, S4_SetStart.Pin_1, S4_SetStart.Pin_2, S5_SetStart1.Pin_3, S5_SetStart1.Pin_4, S6_SetNoThru.Pin_1, S6_SetNoThru.Pin_2, S7_SetThru.Pin_3, S7_SetThru.Pin_4, S8_Restore.Pin_3, S8_Restore.Pin_4
  N16: Arduino_Nano_Rev_3_or_4.D2, S2_SetDIN48.Pin_3, S2_SetDIN48.Pin_4
  N17: Arduino_Nano_Rev_3_or_4.D3, S3_SetDIN24.Pin_1, S3_SetDIN24.Pin_2
  N18: Arduino_Nano_Rev_3_or_4.D5, S4_SetStart.Pin_3, S4_SetStart.Pin_4
  N19: Arduino_Nano_Rev_3_or_4.D6, S5_SetStart1.Pin_1, S5_SetStart1.Pin_2
  N20: Arduino_Nano_Rev_3_or_4.D7, S6_SetNoThru.Pin_3, S6_SetNoThru.Pin_4
  N21: Arduino_Nano_Rev_3_or_4.D12/MISO, S7_SetThru.Pin_1, S7_SetThru.Pin_2
  N22: Arduino_Nano_Rev_3_or_4.RESET, S1_Reset.Pin_1, S1_Reset.Pin_2
  N23: Arduino_Nano_Rev_3_or_4.D13/SCK, S8_Restore.Pin_1, S8_Restore.Pin_2

notes:
  RX
  KentonKontrol V1.0
  by Filthynoises Music
  (No rights reserved)

custom parts:
  6n137 Optocoupler: 6n137 fast Optocoupler. With 8 pins on a 300mil dual inline package (DIP) footprint. Ve is strobe input. Output is inverting.

// code stored in the sketch: KentonControlV1.ino
#include <Control_Surface.h> // Include the Control Surface library


// Select the serial port to use.
auto &serial = Serial;
// Instantiate a Serial MIDI interface at the default MIDI baud rate.
SerialMIDI_Interface<decltype(serial)> midi {serial, MIDI_BAUD};


//  sysex messages to be assigned to buttons
uint8_t sysexDIN48[]   {0xF0, 0x00, 0x20, 0x13, 0x16, 0x00, 0x20, 0x00, 0x02, 0x00, 0x01, 0xF7};
uint8_t sysexDIN24[]   {0xF0, 0x00, 0x20, 0x13, 0x16, 0x00, 0x20, 0x00, 0x02, 0x00, 0x00, 0xF7};
uint8_t sysexStart[]   {0xF0, 0x00, 0x20, 0x13, 0x16, 0x00, 0x20, 0x00, 0x02, 0x00, 0x01, 0xF7};
uint8_t sysexCont[]    {0xF0, 0x00, 0x20, 0x13, 0x16, 0x00, 0x20, 0x00, 0x02, 0x00, 0x00, 0xF7};
uint8_t sysexThruOn[]  {0xF0, 0x00, 0x20, 0x13, 0x16, 0x00, 0x20, 0x00, 0x02, 0x00, 0x01, 0xF7};
uint8_t sysexThruOff[] {0xF0, 0x00, 0x20, 0x13, 0x16, 0x00, 0x20, 0x00, 0x02, 0x00, 0x00, 0xF7};
uint8_t sysexRestore[] {0xF0, 0x00, 0x20, 0x13, 0x16, 0x00, 0x20, 0x00, 0x02, 0x00, 0x00, 0xF7};


// Instantiate Button objects
Button sysexDIN48Button   {2};
Button sysexDIN24Button   {3};
Button sysexStartButton   {5};
Button sysexContButton    {6};
Button sysexThruOnButton  {7};
Button sysexThruOffButton {12};
Button sysexRestoreButton {13};


void setup() {
  Control_Surface.begin(); // Initialize the Control Surface
}


void loop() {
  //  Assign MIDI commands to Buttons
  if (sysexDIN48Button.update()   == Button::Falling) midi.sendSysEx(sysexDIN48);
  if (sysexDIN24Button.update()   == Button::Falling) midi.sendSysEx(sysexDIN24);
  if (sysexStartButton.update()   == Button::Falling) midi.sendSysEx(sysexStart);
  if (sysexContButton.update()    == Button::Falling) midi.sendSysEx(sysexCont);
  if (sysexThruOnButton.update()  == Button::Falling) midi.sendSysEx(sysexThruOn);
  if (sysexThruOffButton.update() == Button::Falling) midi.sendSysEx(sysexThruOff);
  if (sysexRestoreButton.update() == Button::Falling) midi.sendSysEx(sysexRestore);


  //  Send selected MIDI command
  midi.update();
}
